# Fritzing sketch BluetoothModul2 (saved by Fritzing 0.9.2b)
circuit board: 4cm x 2cm
breadboards: 1

parts:
  U1 = BLUETOOTH-HC05 [package=hc05]
  R2 = Resistor [tolerance=±5% resistance=1k package=THT]
  R1 = Resistor [tolerance=±5% resistance=680 package=THT]
  R3 = Resistor [tolerance=±5% resistance=1k package=THT]
  J5 = Resistor [tolerance=±5% resistance=0 package="0603 [SMD]"]
  J6 = Resistor [tolerance=±5% resistance=0 package="0603 [SMD]"]
  LED1 = LED - 3mm [color="Green (560nm)" package="3 mm [THT]"]
  J1 = female pin header, 5 pins [form="♀ (female)"]
  Key = Resistor [tolerance=±5% resistance=0 package="0603 [SMD]"]
  J10 = Resistor [tolerance=±5% resistance=0 package="0603 [SMD]"]

nets:
  N1: U1.UARTTX#0, J1.pin3
  N2: U1.UARTTX#1, R2.Pin_0, R1.Pin_1
  N3: U1.VDD, J1.pin4
  GND: U1.GND, U1.GND1, U1.GND2, R2.Pin_1, LED1.cathode, J1.pin5
  N4: U1.PIO1, J6.Pin_0
  N5: U1.PIO3, J10.Pin_1
  N6: U1.PIO8, J5.Pin_0
  N7: U1.PIO11, Key.Pin_1
  N8: R1.Pin_0, J1.pin2
  N9: R3.Pin_0, J5.Pin_1, J6.Pin_1
  N10: R3.Pin_1, LED1.anode
  N11: J1.pin1, Key.Pin_0, J10.Pin_0

notes:
  bt-v1
  GND
  VCC
  D1
  D2
  A1
  HC-05: J5, Key
  HC-06: J6
  HC-10: J10

custom parts:
  BLUETOOTH-HC05: Bluetooth SMD module
